# Fritzing sketch blink (saved by Fritzing 0.8.5b)
breadboards: 1

parts:
  Componente1 = Arduino Uno (Rev3)
  LED1 = LED - 5mm [color="Blue (470nm)" package="5 mm [THT]"]
  R1 = Resistor [tolerance=±5% resistance=220 package=THT]  # not connected

nets:
  N1: Componente1.D13/SCK, LED1.cathode
  N2: Componente1.GND, LED1.anode
